// Logisim project AVR2.circ as structural Verilog: 7 circuits, main circuit AVRCore
module AVRCore (
);

  wire [7:0] progcounter_1_bus_1_out, progcounter_1_bus_2_out;
  wire [15:0] flash_1_flash_out, instrreg_1_out, instrreg_1_to_dec, progcounter_1_pc_out;
  wire [31:0] decoder_1_ctrl_out;

  // Probe on progcounter_1_bus_1_out
  ProgCounter progcounter_1 (
    .Ctrl_IN(decoder_1_ctrl_out), .Instr_IN(instrreg_1_out), .Bus_1_IN(progcounter_1_bus_1_out),
    .Bus_2_IN(progcounter_1_bus_2_out), .Bus_1_OUT(progcounter_1_bus_1_out),
    .Bus_2_OUT(progcounter_1_bus_2_out), .PC_OUT(progcounter_1_pc_out));  // open: PC_2_OUT, IN
  // Probe on progcounter_1_bus_2_out
  // Probe on instrreg_1_out
  InstrReg instrreg_1 (.Instr_IN(flash_1_flash_out), .TO_DEC(instrreg_1_to_dec), .OUT(instrreg_1_out));
  Flash flash_1 (.PC_IN(progcounter_1_pc_out), .Flash_OUT(flash_1_flash_out));
  Decoder decoder_1 (.Instr_IN(instrreg_1_to_dec), .Ctrl_OUT(decoder_1_ctrl_out));
  // Probe on decoder_1_ctrl_out
endmodule

// FLASH
module Flash (
  input  [15:0] PC_IN,
  output [15:0] Flash_OUT
);

  ROM #(.addrWidth(16), .dataWidth(16)) rom_1 (.addr(PC_IN), .data(Flash_OUT));  // open: sel
endmodule

// DEC
module Decoder (
  input  [15:0] Instr_IN,
  output [31:0] Ctrl_OUT
);

  wire clock_1_out, comparator_1_eq;
  wire [7:0] controlled_buffer_1_out;
  wire [15:0] register_1_q;

  Register #(.width(16)) register_1 (.D(Instr_IN), .en(Ctrl_OUT[0]), .Q(register_1_q), .clk(clock_1_out));  // open: clr
  Clock clock_1 (.out(clock_1_out));
  Comparator #(.width(16), .mode("unsigned")) comparator_1 (
    .a(register_1_q), .b({16{1'b0}}), .eq(comparator_1_eq));  // open: gt, lt
  assign controlled_buffer_1_out = comparator_1_eq ? {8{1'b0}} : 8'bz;  // Controlled_Buffer controlled_buffer_1
  ROM #(.dataWidth(32)) rom_1 (.addr(controlled_buffer_1_out), .data(Ctrl_OUT));  // open: sel
endmodule

// INSTR
module InstrReg (
  input  [15:0] Instr_IN,
  output [15:0] OUT,
  output [15:0] TO_DEC
);

  wire clock_1_out;

  Clock clock_1 (.out(clock_1_out));
  Register #(.width(16), .trigger("high")) register_1 (.D(Instr_IN), .Q(OUT), .clk(clock_1_out));  // open: en, clr

  assign TO_DEC = OUT;
endmodule

// PC
module ProgCounter (
  input  [31:0] Ctrl_IN,
  input  [15:0] Instr_IN,
  input  [7:0] Bus_1_IN,
  input  [7:0] Bus_2_IN,
  input  [15:0] IN,
  output [7:0] Bus_1_OUT,
  output [7:0] Bus_2_OUT,
  output [15:0] PC_2_OUT,
  output [15:0] PC_OUT
);

  wire B1O, B2O, clock_1_out, or_1_out;
  wire [15:0] adder_2_out, adder_3_out, pull_resistor_1_node;

  Pull_Resistor pull_resistor_1 (.node(pull_resistor_1_node));
  Clock clock_1 (.out(clock_1_out));
  Adder #(.width(16)) adder_1 (.a({PC_OUT[15:8], Bus_1_IN}), .b(16'h1), .out(PC_2_OUT));  // open: cin, cout
  assign pull_resistor_1_node = Ctrl_IN[2] ? {Bus_1_IN, Bus_1_IN} : 16'bz;  // Controlled_Buffer controlled_buffer_1
  assign pull_resistor_1_node = Ctrl_IN[1] ? {PC_OUT[15:8], Bus_1_IN} : 16'bz;  // Controlled_Buffer controlled_buffer_2
  assign pull_resistor_1_node = Ctrl_IN[3] ? IN : 16'bz;  // Controlled_Buffer controlled_buffer_3
  Counter #(.width(16), .max('hffff)) counter_1 (
    .load(or_1_out), .D(pull_resistor_1_node), .count(Ctrl_IN[0]), .Q({PC_OUT[15:8], Bus_1_IN}),
    .clk(clock_1_out));  // open: carry, clr
  or or_1 (or_1_out, Ctrl_IN[1], Ctrl_IN[2], Ctrl_IN[3], Ctrl_IN[4]);
  assign pull_resistor_1_node = Ctrl_IN[4] ? adder_3_out : 16'bz;  // Controlled_Buffer controlled_buffer_4
  Adder #(.width(16)) adder_2 (.a({PC_OUT[15:8], Bus_1_IN}), .b(16'h1), .out(adder_2_out));  // open: cin, cout
  Adder #(.width(16)) adder_3 (.a(IN), .b(adder_2_out), .out(adder_3_out));  // open: cin, cout
  Pull_Resistor pull_resistor_2 (.node(Bus_1_OUT));
  Controlled_Buffer #(.width(8)) controlled_buffer_5 (.out(Bus_1_OUT), .en(B1O));  // open: in
  Pull_Resistor pull_resistor_3 (.node(B1O));
  Pull_Resistor pull_resistor_4 (.node(Bus_2_OUT));
  Controlled_Buffer #(.width(8)) controlled_buffer_6 (.out(Bus_2_OUT), .en(B2O));  // open: in
  Pull_Resistor pull_resistor_5 (.node(B2O));

  assign PC_OUT[7:0] = Bus_1_IN;
endmodule

module Device (
  input  [31:0] Ctrl_IN,
  input  [15:0] Instr_IN,
  input  [7:0] Bus_1_IN,
  input  [7:0] Bus_2_IN,
  output [7:0] Bus_1_OUT,
  output [7:0] Bus_2_OUT
);

  wire B1O, B2O;

  Pull_Resistor pull_resistor_1 (.node(Bus_1_OUT));
  Controlled_Buffer #(.width(8)) controlled_buffer_1 (.out(Bus_1_OUT), .en(B1O));  // open: in
  Pull_Resistor pull_resistor_2 (.node(B1O));
  Pull_Resistor pull_resistor_3 (.node(Bus_2_OUT));
  Controlled_Buffer #(.width(8)) controlled_buffer_2 (.out(Bus_2_OUT), .en(B2O));  // open: in
  Pull_Resistor pull_resistor_4 (.node(B2O));
endmodule

module RegFile (
  input  [31:0] Ctrl_IN,
  input  [15:0] Instr_IN,
  input  [7:0] Bus_1_IN,
  input  [7:0] Bus_2_IN,
  output [7:0] Bus_1_OUT,
  output [7:0] Bus_2_OUT,
  output [7:0] ALU_1,
  output [7:0] ALU_2
);

  wire B1O, B2O, r0rd, r0rr, r0w, r1rd, r1rr, r1w, r2rd, r2rr, r2w, r3rd, r3rr, r3w, r4rd, r4rr, r4w, r5rd,
       r5rr, r6rd, r6rr, r6w, r7rd, r7rr, r7w, r8rd, r8rr, r8w, r9rd, r9rr, r9w, r10rd, r10rr, r10w, r11rd,
       r11rr, r11w, r12rd, r12rr, r12w, r13rd, r13rr, r13w, r14rd, r14rr, r14w, r15rd, r15rr, r15w;
  wire [7:0] controlled_buffer_2_out, controlled_buffer_5_out, controlled_buffer_8_out,
       controlled_buffer_11_out, controlled_buffer_14_out, controlled_buffer_17_out,
       controlled_buffer_20_out, controlled_buffer_23_out, controlled_buffer_25_out,
       controlled_buffer_26_out, controlled_buffer_27_out, controlled_buffer_28_out,
       controlled_buffer_29_out, controlled_buffer_30_out, controlled_buffer_31_out,
       controlled_buffer_32_out, controlled_buffer_49_out, controlled_buffer_50_out,
       controlled_buffer_51_out, controlled_buffer_52_out, controlled_buffer_53_out,
       controlled_buffer_54_out, controlled_buffer_55_out, controlled_buffer_56_out,
       controlled_buffer_73_out, controlled_buffer_74_out, controlled_buffer_75_out,
       controlled_buffer_76_out, controlled_buffer_77_out, controlled_buffer_78_out,
       controlled_buffer_79_out, controlled_buffer_80_out, register_1_q, register_2_q, register_3_q,
       register_4_q, register_5_q, register_6_q, register_7_q, register_8_q, register_9_q, register_10_q,
       register_11_q, register_12_q, register_13_q, register_14_q, register_15_q, register_16_q,
       register_17_q, register_18_q, register_19_q, register_20_q, register_21_q, register_22_q,
       register_23_q, register_24_q, register_25_q, register_26_q, register_27_q, register_28_q,
       register_29_q, register_30_q, register_31_q, register_32_q;

  assign ALU_2 = r0rr ? register_1_q : 8'bz;  // Controlled_Buffer controlled_buffer_1
  assign controlled_buffer_2_out = r0w ? Bus_1_IN : 8'bz;  // Controlled_Buffer controlled_buffer_2
  Register register_1 (.D(controlled_buffer_2_out), .en(r0w), .Q(register_1_q));  // open: clk, clr
  assign ALU_1 = r0rd ? register_1_q : 8'bz;  // Controlled_Buffer controlled_buffer_3
  assign ALU_2 = r4rr ? register_2_q : 8'bz;  // Controlled_Buffer controlled_buffer_4
  assign controlled_buffer_5_out = r4w ? Bus_1_IN : 8'bz;  // Controlled_Buffer controlled_buffer_5
  Register register_2 (.D(controlled_buffer_5_out), .en(r4w), .Q(register_2_q));  // open: clk, clr
  assign ALU_1 = r4rd ? register_2_q : 8'bz;  // Controlled_Buffer controlled_buffer_6
  assign ALU_2 = r8rr ? register_3_q : 8'bz;  // Controlled_Buffer controlled_buffer_7
  assign controlled_buffer_8_out = r8w ? Bus_1_IN : 8'bz;  // Controlled_Buffer controlled_buffer_8
  Register register_3 (.D(controlled_buffer_8_out), .en(r8w), .Q(register_3_q));  // open: clk, clr
  assign ALU_1 = r8rd ? register_3_q : 8'bz;  // Controlled_Buffer controlled_buffer_9
  assign ALU_2 = r12rr ? register_4_q : 8'bz;  // Controlled_Buffer controlled_buffer_10
  assign controlled_buffer_11_out = r12w ? Bus_1_IN : 8'bz;  // Controlled_Buffer controlled_buffer_11
  Register register_4 (.D(controlled_buffer_11_out), .en(r12w), .Q(register_4_q));  // open: clk, clr
  assign ALU_1 = r12rd ? register_4_q : 8'bz;  // Controlled_Buffer controlled_buffer_12
  assign ALU_2 = r0rr ? register_5_q : 8'bz;  // Controlled_Buffer controlled_buffer_13
  Register register_5 (.D(controlled_buffer_14_out), .en(r0w), .Q(register_5_q));  // open: clk, clr
  assign controlled_buffer_14_out = r0w ? Bus_1_IN : 8'bz;  // Controlled_Buffer controlled_buffer_14
  assign ALU_1 = r0rd ? register_5_q : 8'bz;  // Controlled_Buffer controlled_buffer_15
  assign ALU_2 = r0rr ? register_6_q : 8'bz;  // Controlled_Buffer controlled_buffer_16
  Register register_6 (.D(controlled_buffer_17_out), .en(r0w), .Q(register_6_q));  // open: clk, clr
  assign controlled_buffer_17_out = r0w ? Bus_1_IN : 8'bz;  // Controlled_Buffer controlled_buffer_17
  assign ALU_1 = r0rd ? register_6_q : 8'bz;  // Controlled_Buffer controlled_buffer_18
  assign ALU_2 = r0rr ? register_7_q : 8'bz;  // Controlled_Buffer controlled_buffer_19
  assign controlled_buffer_20_out = r0w ? Bus_1_IN : 8'bz;  // Controlled_Buffer controlled_buffer_20
  Register register_7 (.D(controlled_buffer_20_out), .en(r0w), .Q(register_7_q));  // open: clk, clr
  assign ALU_1 = r0rd ? register_7_q : 8'bz;  // Controlled_Buffer controlled_buffer_21
  assign ALU_2 = r0rr ? register_8_q : 8'bz;  // Controlled_Buffer controlled_buffer_22
  Register register_8 (.D(controlled_buffer_23_out), .en(r0w), .Q(register_8_q));  // open: clk, clr
  assign controlled_buffer_23_out = r0w ? Bus_1_IN : 8'bz;  // Controlled_Buffer controlled_buffer_23
  assign ALU_1 = r0rd ? register_8_q : 8'bz;  // Controlled_Buffer controlled_buffer_24
  Register register_9 (.D(controlled_buffer_25_out), .en(r1w), .Q(register_9_q));  // open: clk, clr
  assign controlled_buffer_25_out = r1w ? Bus_1_IN : 8'bz;  // Controlled_Buffer controlled_buffer_25
  Register register_10 (.D(controlled_buffer_26_out), .en(r0w), .Q(register_10_q));  // open: clk, clr
  assign controlled_buffer_26_out = r0w ? Bus_1_IN : 8'bz;  // Controlled_Buffer controlled_buffer_26
  assign controlled_buffer_27_out = r9w ? Bus_1_IN : 8'bz;  // Controlled_Buffer controlled_buffer_27
  Register register_11 (.D(controlled_buffer_27_out), .en(r9w), .Q(register_11_q));  // open: clk, clr
  Register register_12 (.D(controlled_buffer_28_out), .en(r13w), .Q(register_12_q));  // open: clk, clr
  assign controlled_buffer_28_out = r13w ? Bus_1_IN : 8'bz;  // Controlled_Buffer controlled_buffer_28
  Register register_13 (.D(controlled_buffer_29_out), .en(r0w), .Q(register_13_q));  // open: clk, clr
  assign controlled_buffer_29_out = r0w ? Bus_1_IN : 8'bz;  // Controlled_Buffer controlled_buffer_29
  Register register_14 (.D(controlled_buffer_30_out), .en(r0w), .Q(register_14_q));  // open: clk, clr
  assign controlled_buffer_30_out = r0w ? Bus_1_IN : 8'bz;  // Controlled_Buffer controlled_buffer_30
  Register register_15 (.D(controlled_buffer_31_out), .en(r0w), .Q(register_15_q));  // open: clk, clr
  assign controlled_buffer_31_out = r0w ? Bus_1_IN : 8'bz;  // Controlled_Buffer controlled_buffer_31
  Register register_16 (.D(controlled_buffer_32_out), .en(r0w), .Q(register_16_q));  // open: clk, clr
  assign controlled_buffer_32_out = r0w ? Bus_1_IN : 8'bz;  // Controlled_Buffer controlled_buffer_32
  assign ALU_2 = r1rr ? register_9_q : 8'bz;  // Controlled_Buffer controlled_buffer_33
  assign ALU_1 = r1rd ? register_9_q : 8'bz;  // Controlled_Buffer controlled_buffer_34
  assign ALU_2 = r5rr ? register_10_q : 8'bz;  // Controlled_Buffer controlled_buffer_35
  assign ALU_1 = r5rd ? register_10_q : 8'bz;  // Controlled_Buffer controlled_buffer_36
  assign ALU_2 = r9rr ? register_11_q : 8'bz;  // Controlled_Buffer controlled_buffer_37
  assign ALU_1 = r9rd ? register_11_q : 8'bz;  // Controlled_Buffer controlled_buffer_38
  assign ALU_2 = r13rr ? register_12_q : 8'bz;  // Controlled_Buffer controlled_buffer_39
  assign ALU_1 = r13rd ? register_12_q : 8'bz;  // Controlled_Buffer controlled_buffer_40
  assign ALU_2 = r0rr ? register_13_q : 8'bz;  // Controlled_Buffer controlled_buffer_41
  assign ALU_1 = r0rd ? register_13_q : 8'bz;  // Controlled_Buffer controlled_buffer_42
  assign ALU_2 = r0rr ? register_14_q : 8'bz;  // Controlled_Buffer controlled_buffer_43
  assign ALU_1 = r0rd ? register_14_q : 8'bz;  // Controlled_Buffer controlled_buffer_44
  assign ALU_2 = r0rr ? register_15_q : 8'bz;  // Controlled_Buffer controlled_buffer_45
  assign ALU_1 = r0rd ? register_15_q : 8'bz;  // Controlled_Buffer controlled_buffer_46
  assign ALU_2 = r0rr ? register_16_q : 8'bz;  // Controlled_Buffer controlled_buffer_47
  assign ALU_1 = r0rd ? register_16_q : 8'bz;  // Controlled_Buffer controlled_buffer_48
  assign controlled_buffer_49_out = r2w ? Bus_1_IN : 8'bz;  // Controlled_Buffer controlled_buffer_49
  assign controlled_buffer_50_out = r6w ? Bus_1_IN : 8'bz;  // Controlled_Buffer controlled_buffer_50
  assign controlled_buffer_51_out = r10w ? Bus_1_IN : 8'bz;  // Controlled_Buffer controlled_buffer_51
  assign controlled_buffer_52_out = r14w ? Bus_1_IN : 8'bz;  // Controlled_Buffer controlled_buffer_52
  assign controlled_buffer_53_out = r0w ? Bus_1_IN : 8'bz;  // Controlled_Buffer controlled_buffer_53
  assign controlled_buffer_54_out = r0w ? Bus_1_IN : 8'bz;  // Controlled_Buffer controlled_buffer_54
  assign controlled_buffer_55_out = r0w ? Bus_1_IN : 8'bz;  // Controlled_Buffer controlled_buffer_55
  assign controlled_buffer_56_out = r0w ? Bus_1_IN : 8'bz;  // Controlled_Buffer controlled_buffer_56
  assign ALU_2 = r2rr ? register_17_q : 8'bz;  // Controlled_Buffer controlled_buffer_57
  Register register_17 (.D(controlled_buffer_49_out), .en(r2w), .Q(register_17_q));  // open: clk, clr
  assign ALU_1 = r2rd ? register_17_q : 8'bz;  // Controlled_Buffer controlled_buffer_58
  assign ALU_2 = r6rr ? register_18_q : 8'bz;  // Controlled_Buffer controlled_buffer_59
  Register register_18 (.D(controlled_buffer_50_out), .en(r6w), .Q(register_18_q));  // open: clk, clr
  assign ALU_1 = r6rd ? register_18_q : 8'bz;  // Controlled_Buffer controlled_buffer_60
  assign ALU_2 = r10rr ? register_19_q : 8'bz;  // Controlled_Buffer controlled_buffer_61
  Register register_19 (.D(controlled_buffer_51_out), .en(r10w), .Q(register_19_q));  // open: clk, clr
  assign ALU_1 = r10rd ? register_19_q : 8'bz;  // Controlled_Buffer controlled_buffer_62
  assign ALU_2 = r14rr ? register_20_q : 8'bz;  // Controlled_Buffer controlled_buffer_63
  Register register_20 (.D(controlled_buffer_52_out), .en(r14w), .Q(register_20_q));  // open: clk, clr
  assign ALU_1 = r14rd ? register_20_q : 8'bz;  // Controlled_Buffer controlled_buffer_64
  assign ALU_2 = r0rr ? register_21_q : 8'bz;  // Controlled_Buffer controlled_buffer_65
  Register register_21 (.D(controlled_buffer_53_out), .en(r0w), .Q(register_21_q));  // open: clk, clr
  assign ALU_1 = r0rd ? register_21_q : 8'bz;  // Controlled_Buffer controlled_buffer_66
  assign ALU_2 = r0rr ? register_22_q : 8'bz;  // Controlled_Buffer controlled_buffer_67
  Register register_22 (.D(controlled_buffer_54_out), .en(r0w), .Q(register_22_q));  // open: clk, clr
  assign ALU_1 = r0rd ? register_22_q : 8'bz;  // Controlled_Buffer controlled_buffer_68
  assign ALU_2 = r0rr ? register_23_q : 8'bz;  // Controlled_Buffer controlled_buffer_69
  Register register_23 (.D(controlled_buffer_55_out), .en(r0w), .Q(register_23_q));  // open: clk, clr
  assign ALU_1 = r0rd ? register_23_q : 8'bz;  // Controlled_Buffer controlled_buffer_70
  assign ALU_2 = r0rr ? register_24_q : 8'bz;  // Controlled_Buffer controlled_buffer_71
  Register register_24 (.D(controlled_buffer_56_out), .en(r0w), .Q(register_24_q));  // open: clk, clr
  assign ALU_1 = r0rd ? register_24_q : 8'bz;  // Controlled_Buffer controlled_buffer_72
  assign controlled_buffer_73_out = r3w ? Bus_1_IN : 8'bz;  // Controlled_Buffer controlled_buffer_73
  assign controlled_buffer_74_out = r7w ? Bus_1_IN : 8'bz;  // Controlled_Buffer controlled_buffer_74
  assign controlled_buffer_75_out = r11w ? Bus_1_IN : 8'bz;  // Controlled_Buffer controlled_buffer_75
  assign controlled_buffer_76_out = r15w ? Bus_1_IN : 8'bz;  // Controlled_Buffer controlled_buffer_76
  assign controlled_buffer_77_out = r0w ? Bus_1_IN : 8'bz;  // Controlled_Buffer controlled_buffer_77
  assign controlled_buffer_78_out = r0w ? Bus_1_IN : 8'bz;  // Controlled_Buffer controlled_buffer_78
  assign controlled_buffer_79_out = r0w ? Bus_1_IN : 8'bz;  // Controlled_Buffer controlled_buffer_79
  assign controlled_buffer_80_out = r0w ? Bus_1_IN : 8'bz;  // Controlled_Buffer controlled_buffer_80
  assign ALU_2 = r3rr ? register_25_q : 8'bz;  // Controlled_Buffer controlled_buffer_81
  Register register_25 (.D(controlled_buffer_73_out), .en(r3w), .Q(register_25_q));  // open: clk, clr
  assign ALU_1 = r3rd ? register_25_q : 8'bz;  // Controlled_Buffer controlled_buffer_82
  assign ALU_2 = r7rr ? register_26_q : 8'bz;  // Controlled_Buffer controlled_buffer_83
  Register register_26 (.D(controlled_buffer_74_out), .en(r7w), .Q(register_26_q));  // open: clk, clr
  assign ALU_1 = r7rd ? register_26_q : 8'bz;  // Controlled_Buffer controlled_buffer_84
  assign ALU_2 = r11rr ? register_27_q : 8'bz;  // Controlled_Buffer controlled_buffer_85
  Register register_27 (.D(controlled_buffer_75_out), .en(r11w), .Q(register_27_q));  // open: clk, clr
  assign ALU_1 = r11rd ? register_27_q : 8'bz;  // Controlled_Buffer controlled_buffer_86
  assign ALU_2 = r15rr ? register_28_q : 8'bz;  // Controlled_Buffer controlled_buffer_87
  Register register_28 (.D(controlled_buffer_76_out), .en(r15w), .Q(register_28_q));  // open: clk, clr
  assign ALU_1 = r15rd ? register_28_q : 8'bz;  // Controlled_Buffer controlled_buffer_88
  assign ALU_2 = r0rr ? register_29_q : 8'bz;  // Controlled_Buffer controlled_buffer_89
  Register register_29 (.D(controlled_buffer_77_out), .en(r0w), .Q(register_29_q));  // open: clk, clr
  assign ALU_1 = r0rd ? register_29_q : 8'bz;  // Controlled_Buffer controlled_buffer_90
  assign ALU_2 = r0rr ? register_30_q : 8'bz;  // Controlled_Buffer controlled_buffer_91
  Register register_30 (.D(controlled_buffer_78_out), .en(r0w), .Q(register_30_q));  // open: clk, clr
  assign ALU_1 = r0rd ? register_30_q : 8'bz;  // Controlled_Buffer controlled_buffer_92
  assign ALU_2 = r0rr ? register_31_q : 8'bz;  // Controlled_Buffer controlled_buffer_93
  Register register_31 (.D(controlled_buffer_79_out), .en(r0w), .Q(register_31_q));  // open: clk, clr
  assign ALU_1 = r0rd ? register_31_q : 8'bz;  // Controlled_Buffer controlled_buffer_94
  assign ALU_2 = r0rr ? register_32_q : 8'bz;  // Controlled_Buffer controlled_buffer_95
  Register register_32 (.D(controlled_buffer_80_out), .en(r0w), .Q(register_32_q));  // open: clk, clr
  assign ALU_1 = r0rd ? register_32_q : 8'bz;  // Controlled_Buffer controlled_buffer_96
  Pull_Resistor pull_resistor_1 (.node(Bus_1_OUT));
  Controlled_Buffer #(.width(8)) controlled_buffer_97 (.out(Bus_1_OUT), .en(B1O));  // open: in
  Pull_Resistor pull_resistor_2 (.node(B1O));
  Pull_Resistor pull_resistor_3 (.node(Bus_2_OUT));
  Controlled_Buffer #(.width(8)) controlled_buffer_98 (.out(Bus_2_OUT), .en(B2O));  // open: in
  Pull_Resistor pull_resistor_4 (.node(B2O));

  // Other names for the same wires on the sheet: d[7:0] = Bus_1_IN; Rd[7:0] = ALU_1; Rr[7:0] = ALU_2
endmodule
